# Fritzing sketch shieldPCB (saved by Fritzing 0.9.3b)

parts:
  Part1 = Arduino Due (Rev2b)
  M1 = RioRand LM2596  # not connected
  Part2 = Motor Driver 1A Dual TB6612FNG  # not connected
  U1 = LM124-324 Quad Opamp [package="DIP (Dual Inline)"]
  U2 = LM124-324 Quad Opamp [package="DIP (Dual Inline)"]
  U3 = LM124-324 Quad Opamp [package="DIP (Dual Inline)"]
  J1 = Dagu DGServo 9g header (male) [package=THT]
  J3 = Dagu DGServo 9g header (male) [package=THT]
  J4 = Dagu DGServo 9g header (male) [package=THT]
  U4 = POT [package=pot_alpha_rv16af-20]
  J5 = Dagu DGServo 9g header (male) [package=THT]
  S1 = Toggle Switch [package=THT]

nets:
  N1: Part1.DAC0, S1.L1
  N2: Part1.IOREF, U1.VCC+, U2.VCC+, U3.VCC+, U4.A
  N3: Part1.GND, U1.VCC-, U2.VCC-, U3.VCC-, U4.E
  N4: Part1.D30, U3.4OUT
  N5: Part1.D32, U3.3OUT
  N6: Part1.D34, U3.2OUT
  N7: Part1.D36, U3.1OUT
  N8: Part1.D38, U1.4OUT
  N9: Part1.D40, U1.3OUT
  N10: Part1.D42, U1.2OUT
  N11: Part1.D44, U1.1OUT
  N12: Part1.D46, U2.4OUT
  N13: Part1.D48, U2.1OUT
  N14: Part1.D50, U2.2OUT
  N15: Part1.D52, U2.3OUT
  N16: U1.1IN-, U1.2IN-, U1.3IN-, U1.4IN-, U2.1IN-, U2.2IN-, U2.3IN-, U2.4IN-, U3.1IN-, U3.2IN-, U3.3IN-, U3.4IN-, S1.COM
  N17: U1.1IN+, J3.gnd
  N18: U1.2IN+, J3.Vcc
  N19: U1.3IN+, J5.pulse
  N20: U1.4IN+, J5.Vcc
  N21: U2.1IN+, J4.pulse
  N22: U2.2IN+, J4.Vcc
  N23: U2.3IN+, J3.pulse
  N24: U2.4IN+, J4.gnd
  N25: U3.1IN+, J5.gnd
  N26: U3.2IN+, J1.pulse
  N27: U3.3IN+, J1.Vcc
  N28: U3.4IN+, J1.gnd
  N29: U4.S, S1.L2
