# Fritzing sketch sensors (saved by Fritzing 0.9.3b)
circuit board: 11.1cm x 6.3cm
breadboards: 1

parts:
  T4 = LED - 3mm [color="Red (633nm)" package="3 mm [THT]"]
  R4 = LED - 3mm [color="Red (633nm)" package="3 mm [THT]"]
  T3 = LED - 3mm [color="Red (633nm)" package="3 mm [THT]"]
  R3 = LED - 3mm [color="Red (633nm)" package="3 mm [THT]"]
  R5 = LED - 3mm [color="Red (633nm)" package="3 mm [THT]"]
  T5 = LED - 3mm [color="Red (633nm)" package="3 mm [THT]"]
  R6 = LED - 3mm [color="Red (633nm)" package="3 mm [THT]"]
  T6 = LED - 3mm [color="Red (633nm)" package="3 mm [THT]"]
  R2 = LED - 3mm [color="Red (633nm)" package="3 mm [THT]"]
  T2 = LED - 3mm [color="Red (633nm)" package="3 mm [THT]"]
  R1 = LED - 3mm [color="Red (633nm)" package="3 mm [THT]"]
  T1 = LED - 3mm [color="Red (633nm)" package="3 mm [THT]"]
  R7 = LED - 3mm [color="Red (633nm)" package="3 mm [THT]"]
  T7 = LED - 3mm [color="Red (633nm)" package="3 mm [THT]"]
  R8 = LED - 3mm [color="Red (633nm)" package="3 mm [THT]"]
  T8 = LED - 3mm [color="Red (633nm)" package="3 mm [THT]"]
  R0 = LED - 3mm [color="Red (633nm)" package="3 mm [THT]"]
  T0 = LED - 3mm [color="Red (633nm)" package="3 mm [THT]"]
  R0-8 = female pin header, 9 pins [form="♀ (female)"]
  Power = female pin header, 5 pins [form="♀ (female)"]
  R0_2 = Resistor [tolerance=±5% resistance=10k package=THT]
  R1_2 = Resistor [tolerance=±5% resistance=10k package=THT]
  R2_2 = Resistor [tolerance=±5% resistance=10k package=THT]
  R3_2 = Resistor [tolerance=±5% resistance=10k package=THT]
  R4_2 = Resistor [tolerance=±5% resistance=10k package=THT]
  R5_2 = Resistor [tolerance=±5% resistance=10k package=THT]
  R6_2 = Resistor [tolerance=±5% resistance=10k package=THT]
  R7_2 = Resistor [tolerance=±5% resistance=10k package=THT]
  R8_2 = Resistor [tolerance=±5% resistance=10k package=THT]
  Q1 = TRANSISTOR_NPN [package=to-92]
  Q2 = TRANSISTOR_NPN [package=to-92]
  R9 = Resistor [tolerance=±5% resistance=330 package=THT]

nets:
  N1: T4.cathode, T3.cathode, T5.cathode, T6.cathode, T2.cathode, Q2.C
  N2: T4.anode, T3.anode, T5.anode, T6.anode, T2.anode, T1.anode, T7.anode, T8.anode, T0.anode, R9.Pin_0
  N3: R4.cathode, R3.cathode, R5.cathode, R6.cathode, R2.cathode, R1.cathode, R7.cathode, R8.cathode, R0.cathode, Power.pin1
  N4: R4.anode, R0-8.pin5, R4_2.Pin_1
  N5: R3.anode, R0-8.pin4, R3_2.Pin_1
  N6: R5.anode, R0-8.pin6, R5_2.Pin_1
  N7: R6.anode, R0-8.pin7, R6_2.Pin_1
  N8: R2.anode, R0-8.pin3, R2_2.Pin_1
  N9: R1.anode, R0-8.pin2, R1_2.Pin_1
  N10: T1.cathode, T7.cathode, T8.cathode, T0.cathode, Q1.C
  N11: R7.anode, R0-8.pin8, R7_2.Pin_1
  N12: R8.anode, R0-8.pin9, R8_2.Pin_1
  N13: R0.anode, R0-8.pin1, R0_2.Pin_1
  N14: Power.pin2, R9.Pin_1
  N15: Power.pin3, R0_2.Pin_0, R1_2.Pin_0, R2_2.Pin_0, R3_2.Pin_0, R4_2.Pin_0, R5_2.Pin_0, R6_2.Pin_0, R7_2.Pin_0, R8_2.Pin_0, Q1.E, Q2.E
  N16: Power.pin4, Q1.B
  N17: Power.pin5, Q2.B
